// Logisim project oisc.circ as structural Verilog: 1 circuit, main circuit main
module main (
  input  [7:0] DEBUG_IN
);

  wire and_1_out, CLK, demultiplexer_2_out0, demultiplexer_2_out1, not_1_out, not_2_out, OE_ADDR, OE_ALU,
       OE_DBGIN, OE_DBGOUT, OE_IO, OE_MEM, OE_PC, OE_RAM, OE_ROM, SUFFIX_SELECT, WE_DBGOUT, WE_HADDR, WE_IO,
       WE_LADDR, WE_MEM, WE_PC, WE_RAM, WE_X, WE_Y, Z_DETECT;
  wire [2:0] ADDRESS, SUFFIX_BITS;
  wire [3:0] MICRO_ADDR;
  wire [7:0] buffer_1_out, controlled_buffer_6_out, DATA, HADDR_q, HPC_q, LADDR_q, LPC_q, NOR_out,
       register_1_q, X_q, Y_q;
  wire [15:0] ADDR_DIRECT, rom_2_data;

  Register #(.trigger("high")) X (.D(DATA), .en(1'b1), .Q(X_q), .clk(WE_X));  // open: clr
  Register #(.trigger("high")) Y (.D(DATA), .en(1'b1), .Q(Y_q), .clk(WE_Y));  // open: clr
  Register #(.trigger("high")) HPC (.D(ADDR_DIRECT[15:8]), .Q(HPC_q), .clk(WE_PC));  // open: en, clr
  assign ADDR_DIRECT[15:8] = OE_PC ? HPC_q : 8'bz;  // Controlled_Buffer controlled_buffer_1
  Register #(.trigger("high")) HADDR (.D(DATA), .Q(HADDR_q), .clk(WE_HADDR));  // open: en, clr
  assign ADDR_DIRECT[15:8] = OE_ADDR ? HADDR_q : 8'bz;  // Controlled_Buffer controlled_buffer_2
  assign NOR_out = ~(X_q | Y_q);  // NOR_Gate NOR, 8 bits wide
  assign DATA = OE_ALU ? NOR_out : 8'bz;  // Controlled_Buffer controlled_buffer_3
  assign ADDR_DIRECT[7:0] = OE_PC ? LPC_q : 8'bz;  // Controlled_Buffer controlled_buffer_4
  Register #(.trigger("high")) LPC (.D(ADDR_DIRECT[7:0]), .Q(LPC_q), .clk(WE_PC));  // open: en, clr
  assign ADDR_DIRECT[7:0] = OE_ADDR ? LADDR_q : 8'bz;  // Controlled_Buffer controlled_buffer_5
  Register #(.trigger("high")) LADDR (.D(DATA), .Q(LADDR_q), .clk(WE_LADDR));  // open: en, clr
  Multiplexer #(.width(3), .enable("false")) multiplexer_1 (
    .in0(ADDR_DIRECT[2:0]), .in1(SUFFIX_BITS), .out(ADDRESS), .sel(SUFFIX_SELECT));
  not not_1 (not_1_out, WE_RAM);
  assign buffer_1_out = DATA;  // Buffer buffer_1, 8 bits wide
  assign controlled_buffer_6_out = WE_RAM ? buffer_1_out : 8'bz;  // Controlled_Buffer controlled_buffer_6
  RAM #(.addrWidth(16), .bus("asynch")) ram_1 (
    .addr({ADDR_DIRECT[15:3], ADDRESS}), .data(controlled_buffer_6_out), .ld(not_1_out));  // open: sel, clr
  assign DATA = OE_RAM ? controlled_buffer_6_out : 8'bz;  // Controlled_Buffer controlled_buffer_7
  nor Z (Z_DETECT, NOR_out[0], NOR_out[1], NOR_out[2], NOR_out[3], NOR_out[4], NOR_out[5], NOR_out[6], NOR_out[7]);
  Clock CLK1 (.out(CLK));
  // Probe on DATA
  // Probe on {ADDR_DIRECT[15:3], ADDRESS}
  Pull_Resistor pull_resistor_1 (.node({ADDR_DIRECT[15:3], ADDRESS}));
  Counter #(.width(4), .max('hf)) counter_1 (
    .Q(MICRO_ADDR), .clk(not_2_out), .clr(and_1_out));  // open: load, D, count, carry
  not not_2 (not_2_out, CLK);
  ROM #(.addrWidth(15)) rom_1 (.addr({ADDR_DIRECT[14:3], ADDRESS}), .data(DATA), .sel(OE_ROM));
  and and_1 (and_1_out, MICRO_ADDR[1], MICRO_ADDR[3]);
  ROM #(.addrWidth(5), .dataWidth(16)) rom_2 (
    .addr({Z_DETECT, MICRO_ADDR}),
    .data({rom_2_data[15:12], SUFFIX_SELECT, SUFFIX_BITS, rom_2_data[7], WE_PC, WE_MEM, WE_HADDR, WE_LADDR, WE_X, WE_Y, rom_2_data[0]}),
    .sel(CLK));
  Demultiplexer #(.select(2), .enable("false")) demultiplexer_1 (
    .out2(WE_RAM), .out3(WE_IO), .in(WE_MEM), .sel(ADDR_DIRECT[15:14]));  // open: out0, out1
  Demultiplexer #(.select(2), .enable("false")) demultiplexer_2 (
    .out0(demultiplexer_2_out0), .out1(demultiplexer_2_out1), .out2(OE_RAM), .out3(OE_IO), .in(OE_MEM),
    .sel(ADDR_DIRECT[15:14]));
  Pull_Resistor pull_resistor_2 (.node({rom_2_data[15:12], SUFFIX_SELECT, SUFFIX_BITS, rom_2_data[7], WE_PC, WE_MEM, WE_HADDR, WE_LADDR, WE_X, WE_Y, rom_2_data[0]}));
  or or_1 (OE_ROM, demultiplexer_2_out0, demultiplexer_2_out1);
  buf buffer_2 (OE_ALU, rom_2_data[12]);
  buf buffer_3 (OE_MEM, rom_2_data[13]);
  buf buffer_4 (OE_PC, rom_2_data[14]);
  buf buffer_5 (OE_ADDR, rom_2_data[15]);
  LED led_1 (.in(DEBUG_IN[5]));
  LED led_2 (.in(DEBUG_IN[4]));
  LED led_3 (.in(DEBUG_IN[7]));
  LED led_4 (.in(DEBUG_IN[6]));
  Register #(.trigger("high")) register_1 (.D(DATA), .Q(register_1_q), .clk(WE_DBGOUT));  // open: en, clr
  LED led_5 (.in(register_1_q[7]));
  LED led_6 (.in(register_1_q[6]));
  LED led_7 (.in(register_1_q[4]));
  LED led_8 (.in(register_1_q[5]));
  Demultiplexer #(.enable("false")) demultiplexer_3 (.out0(OE_DBGOUT), .out1(OE_DBGIN), .in(OE_IO), .sel(ADDRESS[0]));
  Demultiplexer #(.enable("false")) demultiplexer_4 (.out0(WE_DBGOUT), .in(WE_IO), .sel(ADDRESS[0]));  // open: out1
  assign DATA = OE_DBGIN ? DEBUG_IN : 8'bz;  // Controlled_Buffer controlled_buffer_8
  LED led_9 (.in(DEBUG_IN[1]));
  LED led_10 (.in(DEBUG_IN[3]));
  LED led_11 (.in(DEBUG_IN[0]));
  LED led_12 (.in(DEBUG_IN[2]));
  assign DATA = OE_DBGOUT ? {8{1'b0}} : 8'bz;  // Controlled_Buffer controlled_buffer_9
  LED led_13 (.in(register_1_q[1]));
  LED led_14 (.in(register_1_q[3]));
  LED led_15 (.in(register_1_q[2]));
  LED led_16 (.in(register_1_q[0]));

  // Other names for the same wires on the sheet: ADDRESS[15:3] = ADDR_DIRECT[15:3]

  // Notes on the sheet:
  //   RAM
  //   ALU
  //   REGISTERS
  //   buffered for data holdoff (caps irl)
  //   PROGRAM ROM
  //   MAPPED MEMORY
  //   contents of rom_1 (hex, n*v repeats v):
  //   bf d0 7d 0 0 8 0 8 bf d0 7d 41 0 10 0 10 bf d1 7d 0 0 18 0 18 bf d1 7d 10 0 20 0 20 bf d2 7d 0 0 28
  //   0 28 bf d2 7d 83 0 30 0 30 bf d3 7d 0 0 38 0 38 bf d3 7d 0 0 40 0 40 bf d4 7d 0 0 48 0 48 bf d4 7d
  //   41 0 50 0 50 bf d5 7d 0 0 58 0 58 bf d5 7d 28 0 60 0 60 bf d6 7d 0 0 68 0 68 bf d6 7d 41 0 70 0 70
  //   bf d7 7d 0 0 78 0 78 bf d7 7d 28 0 80 0 80 bf d8 7d 0 0 88 0 88 bf d8 7d 41 0 90 0 90 bf d9 7d 0 0
  //   98 0 98 bf d9 7d 10 0 a0 0 a0 bf dc 7d 0 0 a8 0 a8 bf dc 7d 41 0 b0 0 b0 bf dd 7d 0 0 b8 0 b8 bf dd
  //   7d 20 0 c0 0 c0 bf de 7d 0 0 c8 0 c8 bf de 7d 41 0 d0 0 d0 bf df 7d 0 0 d8 0 d8 bf df 7d 20 0 e0 0
  //   e0 bf e0 7d 0 0 e8 0 e8 bf e0 7d 41 0 f0 0 f0 bf e1 7d 0 0 f8 0 f8 bf e1 7d f 1 0 1 0 bf e2 7d 0 1 8
  //   1 8 bf e2 7d 83 1 10 1 10 bf e3 7d 0 1 18 1 18 bf e3 7d 0 1 20 1 20 80 3 7d 0 1 28 1 28 80 3 7d 0 1
  //   30 1 30 80 3 80 3 1 38 2 38 bf da 7d 0 1 40 1 40 bf da 7d 40 1 48 1 48 bf db 7d 0 1 50 1 50 bf db 7d
  //   ff 1 58 1 58 bf e6 7d 0 1 60 1 60 bf e6 7d ff 1 68 1 68 bf e7 7d 0 1 70 1 70 bf e7 7d 80 1 78 1 78
  //   80 4 80 4 bf d0 bf d0 bf f0 bf f0 1 88 1 88 80 3 7d 0 1 90 1 90 80 3 bf f0 1 98 1 98 80 3 80 3 1 a0
  //   1 a0 80 2 7d 0 1 a8 1 a8 80 2 80 3 1 b0 1 b0 80 2 80 2 1 b8 1 b8 80 0 7d 0 1 c0 1 c0 80 0 7d ff 1 c8
  //   1 c8 80 1 7d 0 1 d0 1 d0 80 1 7d 20 1 d8 1 d8 80 4 80 4 2 40 2 40 c0 0 7d 0 1 e8 1 e8 80 2 7d 0 1 f0
  //   1 f0 80 2 80 3 1 f8 1 f8 80 2 80 2 2 0 2 0 80 0 7d 0 2 8 2 8 80 0 7d fe 2 10 2 10 80 1 7d 0 2 18 2
  //   18 80 1 7d d8 2 20 2 20 80 4 80 4 2 40 2 40 c0 0 7d 1 2 30 2 30 80 3 80 3 1 20 1 20 80 3 80 3 2 38 2
  //   38 80 5 7d 0 2 48 2 48 80 5 80 2 2 50 2 50 80 5 80 5 2 58 2 d0 bf da 7d 0 2 60 2 60 bf da 7d 83 2 68
  //   2 68 bf db 7d 0 2 70 2 70 bf db 80 2 2 78 2 78 bf db bf db 2 80 2 80 bf e6 7d 0 2 88 2 88 bf e6 7d
  //   fe 2 90 2 90 bf e7 7d 0 2 98 2 98 bf e7 7d 58 2 a0 2 a0 80 5 80 5 bf d0 bf d0 bf f0 bf f0 2 b0 2 b0
  //   80 2 7d 0 2 b8 2 b8 80 2 bf f0 2 c0 2 c0 80 2 80 2 2 c8 2 c8 80 5 80 5 2 40 2 40 bf e6 7d 0 2 d8 2
  //   d8 bf e6 80 0 2 e0 2 e0 bf e6 bf e6 2 e8 2 e8 bf e7 7d 0 2 f0 2 f0 bf e7 80 1 2 f8 2 f8 bf e7 bf e7
  //   3 0 3 0 80 5 80 5 bf e0 bf e0 30968*0 1 2 3 4 5 6 7 8 9 a b c d e f 10 11 12 13 14 15 16 17 18 19 1a
  //   1b 1c 1d 1e 1f 20 21 22 23 24 25 26 27 28 29 2a 2b 2c 2d 2e 2f 30 31 32 33 34 35 36 37 38 39 3a 3b
  //   3c 3d 3e 3f 40 41 42 43 44 45 46 47 48 49 4a 4b 4c 4d 4e 4f 50 51 52 53 54 55 56 57 58 59 5a 5b 5c
  //   5d 5e 5f 60 61 62 63 64 65 66 67 68 69 6a 6b 6c 6d 6e 6f 70 71 72 73 74 75 76 77 78 79 7a 7b 7c 7d
  //   7e 7f 80 81 82 83 84 85 86 87 88 89 8a 8b 8c 8d 8e 8f 90 91 92 93 94 95 96 97 98 99 9a 9b 9c 9d 9e
  //   9f a0 a1 a2 a3 a4 a5 a6 a7 a8 a9 aa ab ac ad ae af b0 b1 b2 b3 b4 b5 b6 b7 b8 b9 ba bb bc bd be bf
  //   c0 c1 c2 c3 c4 c5 c6 c7 c8 c9 ca cb cc cd ce cf d0 d1 d2 d3 d4 d5 d6 d7 d8 d9 da db dc dd de df e0
  //   e1 e2 e3 e4 e5 e6 e7 e8 e9 ea eb ec ed ee ef f0 f1 f2 f3 f4 f5 f6 f7 f8 f9 fa fb fc fd fe ff 0 ff 0
  //   1 2 3 4 5 6 7 8 9 a b c d e f 10 11 12 13 14 15 16 17 18 19 1a 1b 1c 1d 1e 1f 20 21 22 23 24 25 26
  //   27 28 29 2a 2b 2c 2d 2e 2f 30 31 32 33 34 35 36 37 38 39 3a 3b 3c 3d 3e 3f 40 41 42 43 44 45 46 47
  //   48 49 4a 4b 4c 4d 4e 4f 50 51 52 53 54 55 56 57 58 59 5a 5b 5c 5d 5e 5f 60 61 62 63 64 65 66 67 68
  //   69 6a 6b 6c 6d 6e 6f 70 71 72 73 74 75 76 77 78 79 7a 7b 7c 7d 7e 7f 80 81 82 83 84 85 86 87 88 89
  //   8a 8b 8c 8d 8e 8f 90 91 92 93 94 95 96 97 98 99 9a 9b 9c 9d 9e 9f a0 a1 a2 a3 a4 a5 a6 a7 a8 a9 aa
  //   ab ac ad ae af b0 b1 b2 b3 b4 b5 b6 b7 b8 b9 ba bb bc bd be bf c0 c1 c2 c3 c4 c5 c6 c7 c8 c9 ca cb
  //   cc cd ce cf d0 d1 d2 d3 d4 d5 d6 d7 d8 d9 da db dc dd de df e0 e1 e2 e3 e4 e5 e6 e7 e8 e9 ea eb ec
  //   ed ee ef f0 f1 f2 f3 f4 f5 f6 f7 f8 f9 fa fb fc fd fe 0 2 4 6 8 a c e 10 12 14 16 18 1a 1c 1e 20 22
  //   24 26 28 2a 2c 2e 30 32 34 36 38 3a 3c 3e 40 42 44 46 48 4a 4c 4e 50 52 54 56 58 5a 5c 5e 60 62 64
  //   66 68 6a 6c 6e 70 72 74 76 78 7a 7c 7e 80 82 84 86 88 8a 8c 8e 90 92 94 96 98 9a 9c 9e a0 a2 a4 a6
  //   a8 aa ac ae b0 b2 b4 b6 b8 ba bc be c0 c2 c4 c6 c8 ca cc ce d0 d2 d4 d6 d8 da dc de e0 e2 e4 e6 e8
  //   ea ec ee f0 f2 f4 f6 f8 fa fc fe 0 2 4 6 8 a c e 10 12 14 16 18 1a 1c 1e 20 22 24 26 28 2a 2c 2e 30
  //   32 34 36 38 3a 3c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
  //   MICROCODE
  //   contents of rom_2 (hex, n*v repeats v):
  //   6a10 6b08 a002 6810 6908 a004 9020 6c10 6d08 8040 1 5*0 6a10 6b08 a002 6810 6908 a004 9020 6e10 6f08
  //   8040 1
  //   I/O
endmodule
